# Fritzing sketch nonaprs (saved by Fritzing 0.9.1b)
circuit board: 3.22057cm x 6.11844cm
breadboards: 1

parts:
  to_3_5mm = 3.5mm Audio Jack [package=audio-jack]
  Nano = Arduino Nano (Rev3.0)
  D11 = female pin header, 1 pin [form="♀ (female)"]
  D12 = female pin header, 1 pin [form="♀ (female)"]
  RMODIN = Resistor [tolerance=±5% resistance=100k package=THT]
  RMODIN_2 = Resistor [tolerance=±5% resistance=100k package=THT]
  C_IN = Ceramic Capacitor [capacitance=1µF package="100 mil [THT, multilayer]"]
  C_DAC3 = Electrolytic Capacitor [capacitance=4.7µF voltage=50V package="100 mil [THT, electrolytic]"]
  RDAC6 = Resistor [tolerance=±5% resistance=270 package=THT]
  ROUT3 = Resistor [tolerance=±5% resistance=100k package=THT]
  ROUT4 = Resistor [tolerance=±5% resistance=1k package=THT]
  RDAC7 = Resistor [tolerance=±1% resistance=1k package=THT]
  RDAC8 = Resistor [tolerance=±1% resistance=2.2k package=THT]
  RDAC9 = Resistor [tolerance=±1% resistance=3.9k package=THT]
  RDAC10 = Resistor [tolerance=±1% resistance=8.2k package=THT]
  to_2_5mm = 3.5mm Audio Jack [package=audio-jack]
  RPTT = Resistor [tolerance=±5% resistance=10k package=THT]
  3_3V = female pin header, 1 pin [form="♀ (female)"]
  GND = female pin header, 1 pin [form="♀ (female)"]
  2N7000 = MOSFET-NCHANNEL [package=to-92]
  C_DAC4 = Ceramic Capacitor [capacitance=100nF package="100 mil [THT, multilayer]"]

nets:
  N1: to_3_5mm.RIGHT, ROUT3.Pin_1, ROUT4.Pin_1
  GND: to_3_5mm.SLEEVE, Nano.GND, RMODIN.Pin_0, RDAC6.Pin_0, ROUT4.Pin_0, RPTT.Pin_1, GND.pin1, 2N7000.G, C_DAC4.1
  N2: Nano.D3, RPTT.Pin_0, 2N7000.S
  N3: Nano.D4, RDAC10.Pin_0
  N4: Nano.D5, RDAC9.Pin_0
  N5: Nano.D6, RDAC8.Pin_0
  N6: Nano.D7, RDAC7.Pin_0
  N7: Nano.D11/MOSI, D11.pin1
  N8: Nano.D12/MISO, D12.pin1
  N9: Nano.A7, RMODIN.Pin_1, RMODIN_2.Pin_0, C_IN.1
  N10: Nano.AREF, Nano.3V3, RMODIN_2.Pin_1, 3_3V.pin1
  N11: C_IN.0, to_2_5mm.LEFT
  N12: C_DAC3.-, RDAC6.Pin_1, RDAC7.Pin_1, RDAC8.Pin_1, RDAC9.Pin_1, RDAC10.Pin_1, C_DAC4.0
  N13: C_DAC3.+, ROUT3.Pin_0
  N14: to_2_5mm.SLEEVE, 2N7000.D

notes:
  KK6NXK
  NONAPRS v0.6
  to 3.5mm
  to 2.5mm
